# Fritzing sketch fade_two_pins_schematic (saved by Fritzing 0.5.2b)
breadboards: 1

parts:
  R1 = Resistor [resistance=470 package=THT]
  LED1 = Red LED - 5mm [package="5 mm [THT]"]
  R2 = Resistor [resistance=470 package=THT]
  LED2 = Red LED - 5mm [package="5 mm [THT]"]
  Arduino1 = Arduino

nets:
  N1: R1.Pin_0, LED1.anode
  N2: R1.Pin_1, Arduino1.D10
  N3: LED1.cathode, LED2.cathode, Arduino1.GND
  N4: R2.Pin_0, Arduino1.D9
  N5: R2.Pin_1, LED2.anode
