# Fritzing sketch dual_color_led_with_voltage_divider (saved by Fritzing 0.5.2b)
breadboards: 1

parts:
  LED_-_dual_color1 = Red LED - 5mm
  Arduino1 = Arduino
  R1 = Rotary Potentiometer (Small)
  R2 = Resistor [resistance=220 package=THT]

nets:
  N1: LED_-_dual_color1.connector0, R1.wiper
  N2: LED_-_dual_color1.connector1, Arduino1.D9
  N3: Arduino1.GND, R2.Pin_1
  N4: Arduino1.3V3, R1.leg2
  N5: R1.leg1, R2.Pin_0
